// Logisim project CA_INNOVATIVE (1).circ as structural Verilog: 1 circuit, main circuit main
module main (
  input  in_1,
  input  in_2,
  input  [6:0] in_3
);

  wire and_1_out, and_2_out, and_3_out, clock_1_out, comparator_1_eq, comparator_2_eq, decoder_1_out1,
       decoder_1_out2, decoder_1_out3, decoder_1_out4, decoder_1_out5, decoder_1_out6, decoder_2_out1,
       decoder_2_out2, decoder_2_out3, decoder_2_out4, decoder_2_out6, decoder_3_out1, decoder_3_out2,
       decoder_3_out3, decoder_3_out5, decoder_3_out6, decoder_3_out7, multiplexer_1_out, not_1_out,
       or_2_out, or_3_out, or_5_out;
  wire [0:0] or_1_out;
  wire [1:0] decoder_2_out5, rom_1_data_2, rom_1_data_3;
  wire [2:0] rom_1_data_4, rom_1_data_5, rom_1_data_6;
  wire [3:0] or_7_out;
  wire [6:0] adder_1_out, counter_1_q, counter_2_q, multiplexer_2_out, rom_1_data;
  wire [10:0] counter_3_q, counter_4_q, counter_5_q, multiplexer_3_out;
  wire [14:0] counter_6_q;
  wire [15:0] adder_2_out, and_4_out, bit_extender_1_out, multiplexer_4_out, multiplexer_5_out, not_2_out,
       or_8_out, ram_1_data, shifter_1_out, shifter_2_out, subtractor_1_out, xor_1_out;
  wire [15:11] counter_5_q_2;
  wire [15:15] counter_6_q_2;

  Clock clock_1 (.out(clock_1_out));
  not not_1 (not_1_out, rom_1_data_2[1]);
  and and_1 (and_1_out, not_1_out, multiplexer_1_out);
  and and_2 (and_2_out, not_1_out, rom_1_data_2[0], multiplexer_1_out);
  and and_3 (and_3_out, rom_1_data_2[1], rom_1_data_2[0]);
  or or_1 (or_1_out[0], and_3_out, and_1_out);
  Multiplexer #(.select(2)) multiplexer_1 (
    .in0(1'b1), .in1(counter_5_q_2[15]), .in2(comparator_2_eq), .in3(comparator_1_eq),
    .out(multiplexer_1_out), .sel(rom_1_data_3));  // open: en
  Comparator #(.width(16)) comparator_1 (
    .a({counter_6_q_2[15], counter_6_q}), .b({16{1'b0}}), .eq(comparator_1_eq));  // open: gt, lt
  Comparator #(.width(1)) comparator_2 (.a(counter_6_q_2[15]), .b(1'b1), .eq(comparator_2_eq));  // open: gt, lt
  Multiplexer #(.select(2), .width(7)) multiplexer_2 (
    .in0(adder_1_out), .in1(rom_1_data), .in2(counter_1_q), .in3({1'b0, counter_5_q_2[14:11], 2'b00}),
    .out(multiplexer_2_out), .sel({rom_1_data_2[1], or_1_out[0]}));  // open: en
  Counter #(.width(7), .max('h7f)) counter_1 (
    .load(and_2_out), .D(adder_1_out), .count(1'b0), .Q(counter_1_q), .clk(clock_1_out));  // open: carry, clr
  Counter #(.width(7), .max('h7f)) counter_2 (
    .load(1'b1), .D(multiplexer_2_out), .count(in_2), .Q(counter_2_q), .clk(clock_1_out));  // open: carry, clr
  Adder #(.width(7)) adder_1 (.a(7'b0000001), .b(counter_2_q), .out(adder_1_out));  // open: cin, cout
  ROM #(.addrWidth(7), .dataWidth(20)) rom_1 (
    .addr(counter_2_q),
    .data({rom_1_data_6, rom_1_data_5, rom_1_data_4, rom_1_data_3, rom_1_data_2, rom_1_data}));  // open: sel
  or or_2 (or_2_out, decoder_2_out5[1], decoder_2_out5[0], decoder_2_out4);
  or or_3 (or_3_out, decoder_3_out5, decoder_3_out6);
  Multiplexer #(.width(11)) multiplexer_3 (
    .in0(counter_4_q), .in1(counter_5_q), .out(multiplexer_3_out), .sel(decoder_3_out5));  // open: en
  Decoder #(.select(3)) decoder_1 (
    .out1(decoder_1_out1), .out2(decoder_1_out2), .out3(decoder_1_out3), .out4(decoder_1_out4),
    .out5(decoder_1_out5), .out6(decoder_1_out6), .sel(rom_1_data_4));  // open: out0, out7, en
  Counter #(.width(11), .max('h7ff)) counter_3 (
    .load(or_3_out), .D(multiplexer_3_out), .count(1'b0), .Q(counter_3_q), .clk(clock_1_out), .clr(in_1));  // open: carry
  Decoder #(.select(3)) decoder_2 (
    .out1(decoder_2_out1), .out2(decoder_2_out2), .out3(decoder_2_out3), .out4(decoder_2_out4),
    .out5(decoder_2_out5[0]), .out6(decoder_2_out6), .out7(decoder_2_out5[1]), .sel(rom_1_data_5));  // open: out0, en
  Counter #(.width(11), .max('h7ff)) counter_4 (
    .load(decoder_1_out6), .D(counter_3_q), .count(decoder_1_out5), .Q(counter_4_q), .clk(clock_1_out));  // open: carry, clr
  or or_4 (or_7_out[2], decoder_1_out1, decoder_1_out2, decoder_1_out3, decoder_1_out4);
  Decoder #(.select(3)) decoder_3 (
    .out1(decoder_3_out1), .out2(decoder_3_out2), .out3(decoder_3_out3), .out4(or_7_out[3]),
    .out5(decoder_3_out5), .out6(decoder_3_out6), .out7(decoder_3_out7), .sel(rom_1_data_6));  // open: out0, en
  RAM #(.addrWidth(11), .dataWidth(16), .bus("separate")) ram_1 (
    .addr(counter_3_q), .din({counter_5_q_2, counter_5_q}), .data(ram_1_data), .str(decoder_3_out7),
    .clk(clock_1_out), .ld(decoder_2_out4));  // open: sel, clr
  or or_5 (or_5_out, decoder_3_out1, or_7_out[3], decoder_2_out1, decoder_2_out2, decoder_2_out3, or_7_out[2]);
  Multiplexer #(.select(2), .width(16)) multiplexer_4 (
    .in0(ram_1_data), .in1({counter_6_q_2[15], counter_6_q}), .in2(bit_extender_1_out),
    .out(multiplexer_4_out), .sel(decoder_2_out5));  // open: in3, en
  Counter #(.width(16), .max('hffff)) counter_5 (
    .load(or_2_out), .D(multiplexer_4_out), .count(decoder_2_out6), .Q({counter_5_q_2, counter_5_q}),
    .clk(clock_1_out));  // open: carry, clr
  or or_6 (or_7_out[1], decoder_2_out3, decoder_2_out2, decoder_1_out3, decoder_1_out4);
  assign bit_extender_1_out = {{5{1'b0}}, counter_4_q};  // Bit_Extender bit_extender_1
  // Probe on ram_1_data
  or or_7 (or_7_out[0], decoder_1_out2, decoder_2_out3, decoder_2_out1, decoder_1_out4);
  Counter #(.width(16), .max('hffff)) counter_6 (
    .load(or_5_out), .D(multiplexer_5_out), .count(decoder_3_out3), .Q({counter_6_q_2[15], counter_6_q}),
    .clk(clock_1_out), .clr(decoder_3_out2));  // open: carry
  Adder #(.width(16)) adder_2 (
    .a({counter_6_q_2[15], counter_6_q}), .b({counter_5_q_2, counter_5_q}), .out(adder_2_out));  // open: cin, cout
  Subtractor #(.width(16)) subtractor_1 (
    .a({counter_6_q_2[15], counter_6_q}), .b({counter_5_q_2, counter_5_q}), .out(subtractor_1_out));  // open: bin, bout
  assign or_8_out = {counter_6_q_2[15], counter_6_q} | {counter_5_q_2, counter_5_q};  // OR_Gate or_8, 16 bits wide
  assign and_4_out = {counter_6_q_2[15], counter_6_q} & {counter_5_q_2, counter_5_q};  // AND_Gate and_4, 16 bits wide
  assign xor_1_out = {counter_6_q_2[15], counter_6_q} ^ {counter_5_q_2, counter_5_q};  // XOR_Gate xor_1, 16 bits wide
  assign not_2_out = ~{counter_6_q_2[15], counter_6_q};  // NOT_Gate not_2, 16 bits wide
  Shifter #(.width(16)) shifter_1 (.in({counter_6_q_2[15], counter_6_q}), .\dist (4'b0001), .out(shifter_1_out));
  Shifter #(.width(16), .shift("lr")) shifter_2 (
    .in({counter_6_q_2[15], counter_6_q}), .\dist (4'b0001), .out(shifter_2_out));
  Multiplexer #(.select(4), .width(16)) multiplexer_5 (
    .in0(adder_2_out), .in1(subtractor_1_out), .in2(or_8_out), .in3(and_4_out), .in4(xor_1_out),
    .in5(not_2_out), .in6(shifter_1_out), .in7(shifter_2_out), .in8({counter_5_q_2, counter_5_q}),
    .out(multiplexer_5_out), .sel(or_7_out));  // open: in9, in10, in11, in12, in13, in14, in15, en

  // Notes on the sheet:
  //   21BCE269
  //   COMPUTER ARCHITECTURE
  //   Bhavya Shah
  //   MICROPROGRAMMED CONTROL - CU AND ALU DESIGN
  //   SBR
  //   MAP
  //   contents of rom_1 (hex, n*v repeats v):
  //   2c3 10002 20040 40 406 40 2c3 3040 2c3 1400a e0040 40 2c3 2000e 9400f 40 2c3 10012 c040 40 2c3 10016
  //   4040 40 2c3 1001a 9401b 2000e 2c3 1001f 9401f 1012 622 40 2c3 3040 2c3 10026 94027 0 440 640 2c3
  //   3040 2c3 1002f 8040 40 2c3 10032 80040 40 2c3 10036 18490 40 2c3 1003a 2040 40 4*0 c0041 12842 a0180
  //   10044 a0100 9464b 40 2840
  //   Control Memory
  //   load DR
  //   F3
  //   AR
  //   F2
  //   PC
  //   F1
  //   Main Memory
  //   DR
  //   S1-F2(7)
  //   AC
endmodule
